# Fritzing sketch Wiring Schematics (saved by Fritzing 0.9.2b)
breadboards: 2

parts:
  J1 = Basic Servo
  Part1 = Arduino Uno (Rev3) - ICSP  # not connected
  Part2 = Arduino Motor Shield (Rev3)
  Raspberry_Pi1 = Raspberry Pi 2
  M1 = DC Motor
  VCC1 = Battery  # not connected
  LED1 = RGB LED (com. anode, rbg) [package="5 mm [THT]"]
  VCC2 = Battery

nets:
  GND: J1.gnd, Raspberry_Pi1.GND
  N1: J1.pulse, Raspberry_Pi1.GPIO18
  N2: Part2.D3_PWM/A, LED1.green_cathode
  N3: Part2.D5_PWM, LED1.blue_cathode
  N4: Part2.D6_PWM, LED1.common_anode
  N5: Part2.B-, M1.pin_2
  N6: Part2.B+, M1.pin_1
  N7: Part2.VMOT, LED1.red_cathode, VCC2.+
  N8: Part2.GND, VCC2.-

notes:
  8 AA Bateries Here
  Cable from Raspberry Pi -->
  This single LED represents my entire LED strip. My the format for it is:
  + B R G Respectively
  + Is common anode. If you are using common cathode, plug into the Arduino's ground input. Resistors were not needed for my setup. Depending on the LED, resistors may be needed
  Cable from Arduino
  <--
  4 AA Bateries Here
